# Fritzing sketch ocb (saved by Fritzing 0.9.3b)
breadboards: 6

parts:
  Raspberry_Pi_1 = Raspberry Pi 3 [part_number=RPI-3-V1.2]
  Componente2 = Adafruit T-Cobbler Plus [part_number="Adafruit #1989 and #2028"]
  U1 = LM2596 step down module
  Power_plug1 = Power plug
  U3 = Nextion Display [part_number=NX8048T070_011 package=Nextion_LCD]
  R1 = Resistor [tolerance=±5% resistance=4.7k package=THT]
  DS1 = DS18B20 1-Wire Temperature Sensor [part_number=DS18B20]

nets:
  3V3: Raspberry_Pi_1.3v3, Raspberry_Pi_1.3V3, Componente2.+3.3V, Componente2.+3.3V_2, R1.Pin_1, DS1.VDD
  N1: Raspberry_Pi_1.GPIO2, Componente2.SDA
  N2: Raspberry_Pi_1.GPIO3, Componente2.SCL
  N3: Raspberry_Pi_1.GPIO4, Componente2.GPIO4, R1.Pin_0, DS1.DQ
  GND: Raspberry_Pi_1.GND, Componente2.GND, DS1.GND
  N4: Raspberry_Pi_1.GPIO17, Componente2.GPIO17
  N5: Raspberry_Pi_1.GPIO27, Componente2.GPIO27
  N6: Raspberry_Pi_1.GPIO22, Componente2.GPIO22
  N7: Raspberry_Pi_1.GPIO10, Componente2.MOSI
  N8: Raspberry_Pi_1.GPIO9, Componente2.MISO
  N9: Raspberry_Pi_1.GPIO11, Componente2.SCLK
  N10: Raspberry_Pi_1.ID_SD, Componente2.EEDAT
  N11: Raspberry_Pi_1.GPIO5, Componente2.GPIO5
  N12: Raspberry_Pi_1.GPIO6, Componente2.GPIO6
  N13: Raspberry_Pi_1.GPIO13, Componente2.GPIO13
  N14: Raspberry_Pi_1.GPIO19, Componente2.GPIO19
  N15: Raspberry_Pi_1.GPIO26, Componente2.GPIO26
  N16: Raspberry_Pi_1.GPIO21, Componente2.GPIO21
  N17: Raspberry_Pi_1.GPIO20, Componente2.GPIO20
  N18: Raspberry_Pi_1.GPIO16, Componente2.GPIO16
  N19: Raspberry_Pi_1.GPIO12, Componente2.GPIO12
  N20: Raspberry_Pi_1.ID_SC, Componente2.EECLK
  N21: Raspberry_Pi_1.GPIO7, Componente2.CE1
  N22: Raspberry_Pi_1.GPIO8, Componente2.CE0
  N23: Raspberry_Pi_1.GPIO25, Componente2.GPIO25
  N24: Raspberry_Pi_1.GPIO24, Componente2.GPIO24
  N25: Raspberry_Pi_1.GPIO23, Componente2.GPIO23
  N26: Raspberry_Pi_1.GPIO18, Componente2.GPIO18
  N27: Raspberry_Pi_1.GPIO15, Componente2.RXD, U3.TX
  N28: Raspberry_Pi_1.GPIO14, Componente2.TXD, U3.RX
  5V: Raspberry_Pi_1.5V, Componente2.+5V
  N29: U1.IN+, Power_plug1.VCC
  GND_2: U1.IN-, U1.OUT-, Power_plug1.GND, U3.GND
  N30: U1.OUT+, U3.+5v

custom parts:
  Adafruit T-Cobbler Plus: The Raspberry Pi has landed on the Maker World like a 40-GPIO pinned, quad-USB ported, credit card sized bomb of DIY joy. And while you can use most of our great Model B accessories by hooking up our downgrade cable, its probably a good time to upgrade your set up and accessorize using all of the 40 pins. That's why we now carry the Assembled Adafruit Pi T-Cobbler Plus - Breakout + Cable for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
  LM2596 step down module: LM2596 DC-DC step down power supply module 3 A.
  Nextion Display: Nextion NX8048T070_011 Display TFT Display
